# Fritzing sketch smart-radio (saved by Fritzing 0.9.3b)
breadboards: 1

parts:
  WeMos_D1_Mini1 = WeMos D1 Mini
  S1 = Momentary Switch [package=ksa_sealed_tac_switch]
  S2 = Momentary Switch [package=ksa_sealed_tac_switch]
  S3 = Momentary Switch [package=ksa_sealed_tac_switch]

nets:
  N1: WeMos_D1_Mini1.5V, S3.3
  N2: WeMos_D1_Mini1.A0, S3.2
  N3: WeMos_D1_Mini1.D3, S1.4
  N4: WeMos_D1_Mini1.D4, S2.2
  N5: WeMos_D1_Mini1.G, S1.1, S2.3
